# Fritzing sketch RFID Interlock (saved by Fritzing 0.9.3b)

parts:
  Part1 = RFID-RC522-v2
  Part2 = Adafruit Feather HUZZAH ESP8266 [part_number="Adafruit #2821"]
  Part3 = Adafruit NeoPixel FeatherWing [part_number="Adafruit #2945"]
  Part4 = Adafruit PowerRelay Feather Wing [part_number="Adafruit #3191"]
  Part5 = Adafruit FeatherWing Proto [part_number="Adafruit #2884"]

nets:
  N1: Part1.SDA, Part5.K
  N2: Part1.SCK, Part5.F
  N3: Part1.MOSI, Part5.SCK
  N4: Part1.MISO, Part1.IRQ, Part5.MOSI
  GND: Part1.GND, Part5.GND
  N5: Part1.RST, Part5.SCL
  N6: Part1.3.3V, Part5.3V
  N7: Part2.GPIO0, Part3.K
  N8: Part2.GPIO2, Part4.H

custom parts:
  RFID-RC522-v2: A simple China made RFID-RC522 Reader; do check the pin labels, as this is a MFRC522 based clone.
  Adafruit Feather HUZZAH ESP8266: his is the Adafruit Feather HUZZAH ESP8266 - our take on an 'all-in-one' ESP8266 WiFi development board with built in USB and battery charging. Its an ESP8266 WiFi module with all the extras you need, ready to rock! We have other boards in the Feather family, check'em out here. At the Feather HUZZAH's heart is an ESP8266 WiFi microcontroller clocked at 80 MHz and at 3.3V logic. This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
  Adafruit NeoPixel FeatherWing: Put on your sunglasses before staring into these 32 configurable eye-blistering RGB LEDs. Arranged in a 4x8 matrix, each pixel is individually addressable. Only one pin is required to control all the LEDs. On the bottom we have jumpers for the DIN line to any of the I/O pins on a Feather. You can cut the default jumper trace and use any pin you like To make it easy to start, the LEDs are by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
  Adafruit PowerRelay Feather Wing: A Feather board without ambition is a Feather board without FeatherWings! This is the Power Relay FeatherWing. It gives you power to control, and control over power. Put simply, you can now turn on and off lamps, fans, solenoids, and other small appliances that run on up to 250VAC or DC power using any Feather board. Compared to our smaller Relay FeatherWings, this one can handle a beefy 1200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
  Adafruit FeatherWing Proto: This is the FeatherWing Proto - a prototyping add-on for all Feather boards. Using our Feather Stacking Headers or Feather Female Headers you can connect a FeatherWing on top or bottom of your Feather board and let the board take flight! This has a duplicate breakout for each pin on a Feather, as well as a bunch of plain grid proto holes. For GND and 3.3V, we give you a strip of connected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
